# Fritzing sketch Desk_adjustment_diagram (saved by Fritzing 0.9.3b)
breadboards: 1

parts:
  LCD1 = LCD screen
  R1 = Trimmer Potentiometer [maximum_resistance=10kΩ package=THT]
  Part1 = Arduino Uno (Rev3)
  hc-sr1 = hc-sr04
  J1 = Basic Servo
  J2 = Basic Servo

nets:
  GND: LCD1.VSS, LCD1.R/W, LCD1.LED-, R1.leg2, Part1.GND, hc-sr1.GND, J1.gnd, J2.gnd
  VCC: LCD1.VDD, LCD1.LED+, R1.leg1, Part1.5V, hc-sr1.VCC, J1.vcc, J2.vcc
  N1: LCD1.V0, R1.wiper
  N2: LCD1.RS, Part1.D5_PWM
  N3: LCD1.E, Part1.D6_PWM
  N4: LCD1.DB4, Part1.D7
  N5: LCD1.DB5, Part1.D8
  N6: LCD1.DB6, Part1.D9_PWM
  N7: LCD1.DB7, Part1.D10_PWM/SS
  N8: Part1.D11_PWM/MOSI, hc-sr1.Echo
  N9: Part1.D12/MISO, hc-sr1.Trig
  N10: Part1.D2, J2.pulse
  N11: Part1.D3_PWM, J1.pulse
